// Logisim project mul_pipeline_1.circ as structural Verilog: 3 circuits, main circuit main
module main (
  input  reset
);

  wire clk_out;
  wire [3:0] opgen_1_op_3;
  wire [4:0] opgen_1_op_5;
  wire [8:0] mulpipe_1_result;

  Clock sysclk ();  // open: out
  Clock #(.highDuration(4), .lowDuration(4)) clk (.out(clk_out));
  // Probe on opgen_1_op_5
  opgen opgen_1 (.reset(reset), .clk(clk_out), .Op_5(opgen_1_op_5), .Op_3(opgen_1_op_3));
  // Probe on opgen_1_op_3
  mulpipe mulpipe_1 (.Op_5(opgen_1_op_5), .Op_3(opgen_1_op_3), .clk(clk_out), .reset(reset), .result(mulpipe_1_result));
  // Probe on mulpipe_1_result

  // Notes on the sheet:
  //   Attention, votre version de Logisim
  //   ne contient pas de tracker. Si vous
  //   enregistrez votre projet, toutes les
  //   informations du tracker seront
  //   définitivement effacées.
  //   ARO - Labo préparatoire Pipeline
endmodule

module mulpipe (
  input  [4:0] Op_5,
  input  [3:0] Op_3,
  input  clk,
  input  reset,
  output [8:0] result
);

  wire [3:0] register_3_q, register_6_q, register_9_q;
  wire [4:0] multiplexer_1_out, multiplexer_2_out, multiplexer_3_out, multiplexer_4_out, register_2_q,
       register_5_q, register_8_q;
  wire [5:0] adder_1_out, register_1_q;
  wire [6:0] adder_2_out, register_4_q;
  wire [6:6] adder_1_cout;
  wire [7:0] adder_3_out, register_7_q;
  wire [7:7] adder_2_cout;
  wire [8:8] adder_3_cout;

  Multiplexer #(.width(5), .enable("false")) multiplexer_1 (
    .in0({5{1'b0}}), .in1(Op_5), .out(multiplexer_1_out), .sel(Op_3[0]));
  Register #(.width(6)) register_1 (.D({1'b0, multiplexer_1_out}), .en(1'b1), .clk(clk), .Q(register_1_q), .clr(reset));
  Register #(.width(5)) register_2 (.D(Op_5), .en(1'b1), .clk(clk), .Q(register_2_q), .clr(reset));
  Register #(.width(4)) register_3 (.D(Op_3), .en(1'b1), .clk(clk), .Q(register_3_q), .clr(reset));
  // Probe on register_1_q
  Multiplexer #(.width(5), .enable("false")) multiplexer_2 (
    .in0({5{1'b0}}), .in1(register_2_q), .out(multiplexer_2_out), .sel(register_3_q[1]));
  Adder #(.width(6)) adder_1 (
    .a(register_1_q), .b({multiplexer_2_out, 1'b0}), .out(adder_1_out), .cin(1'b0), .cout(adder_1_cout[6]));
  Register #(.width(7)) register_4 (
    .D({adder_1_cout[6], adder_1_out}), .en(1'b1), .clk(clk), .Q(register_4_q), .clr(reset));
  Register #(.width(5)) register_5 (.D(register_2_q), .en(1'b1), .clk(clk), .Q(register_5_q), .clr(reset));
  Register #(.width(4)) register_6 (.D(register_3_q), .en(1'b1), .clk(clk), .Q(register_6_q), .clr(reset));
  // Probe on register_4_q
  Multiplexer #(.width(5), .enable("false")) multiplexer_3 (
    .in0({5{1'b0}}), .in1(register_5_q), .out(multiplexer_3_out), .sel(register_6_q[2]));
  Adder #(.width(7)) adder_2 (
    .a(register_4_q), .b({multiplexer_3_out, 2'b00}), .out(adder_2_out), .cin(1'b0), .cout(adder_2_cout[7]));
  Register register_7 (.D({adder_2_cout[7], adder_2_out}), .en(1'b1), .clk(clk), .Q(register_7_q), .clr(reset));
  Register #(.width(5)) register_8 (.D(register_5_q), .en(1'b1), .clk(clk), .Q(register_8_q), .clr(reset));
  Register #(.width(4)) register_9 (.D(register_6_q), .en(1'b1), .clk(clk), .Q(register_9_q), .clr(reset));
  // Probe on register_7_q
  Multiplexer #(.width(5), .enable("false")) multiplexer_4 (
    .in0({5{1'b0}}), .in1(register_8_q), .out(multiplexer_4_out), .sel(register_9_q[3]));
  Adder adder_3 (
    .a(register_7_q), .b({multiplexer_4_out, 3'b000}), .out(adder_3_out), .cin(1'b0), .cout(adder_3_cout[8]));
  Register #(.width(9)) register_10 (.D({adder_3_cout[8], adder_3_out}), .en(1'b1), .clk(clk), .Q(result), .clr(reset));
  // Probe on nothing

  // Notes on the sheet:
  //   Attention, votre version de Logisim
  //   ne contient pas de tracker. Si vous
  //   enregistrez votre projet, toutes les
  //   informations du tracker seront
  //   définitivement effacées.
  //   Sélection si op3[0] = 1
  //   Sélection si op3[1] = 1
  //   mult par 2
  //   Sélection si op3[2] = 1
  //   mult par 4
  //   mult par 8
endmodule

module opgen (
  input  reset,
  input  clk,
  output [4:0] Op_5,
  output [3:0] Op_3
);

  wire [2:0] counter_1_q;

  Counter #(.width(3), .max('h7)) counter_1 (
    .clr(reset), .load(1'b0), .up(1'b1), .count(1'b1), .clk(clk), .Q(counter_1_q));  // open: D, carry
  ROM #(.addrWidth(3), .dataWidth(5)) vect_op_5 (.addr(counter_1_q), .data(Op_5));
  ROM #(.addrWidth(3), .dataWidth(4)) vect_op_4 (.addr(counter_1_q), .data(Op_3));

  // Notes on the sheet:
  //   Attention, votre version de Logisim
  //   ne contient pas de tracker. Si vous
  //   enregistrez votre projet, toutes les
  //   informations du tracker seront
  //   définitivement effacées.
  //   contents of vect_op_5 (hex, n*v repeats v):
  //   5 7 9 1e
  //   contents of vect_op_4 (hex, n*v repeats v):
  //   f 4 7 7
endmodule
